# Fritzing sketch circuid (saved by Fritzing 0.9.3b)
breadboards: 1

parts:
  S2 = Momentary Switch [package=ksa_sealed_tac_switch]
  S3 = Momentary Switch [package=ksa_sealed_tac_switch]
  S4 = Momentary Switch [package=ksa_sealed_tac_switch]
  MKR1 = Arduino MKR1000
  Grove1 = Grove 4 Digit Display
  U2 = SUP500F [package=sup500f]
  R1 = Resistor [tolerance=±5% resistance=220 package=THT]
  LED1 = LED - 3mm [color="Red (633nm)" package="3 mm [THT]"]

nets:
  GND: S2.2, S3.2, S4.2, MKR1.GND, Grove1.GND, U2.GND, R1.Pin_1
  N1: S2.4, MKR1.D4_PWM
  N2: S3.4, MKR1.1
  N3: S4.4, MKR1.0
  N4: MKR1.D2_PWM, LED1.anode
  VCC: MKR1.VCC, Grove1.VCC, U2.VCC
  N5: MKR1.14/TX, U2.RX-I
  N6: MKR1.13/RX, U2.TX-O
  N7: MKR1.8/MOSI, Grove1.CLK
  N8: MKR1.7, Grove1.DIO
  N9: R1.Pin_0, LED1.cathode
